// Logisim project myCPU.circ as structural Verilog: 9 circuits, main circuit main
module main (
);

  wire alu_1_out_5, dram_1_out_4, irom_1_out_2, multiplexer_1_out, multiplexer_2_out, multiplexer_3_out,
       npc_1_out_5, npc_1_out_6, pc_1_out_2, rf_1_out_6, rf_1_out_7, sext_1_out_3;

  NPC npc_1 (
    .in_1(pc_1_out_2), .in_2(sext_1_out_3), .in_3(rf_1_out_6), .out_5(npc_1_out_5), .out_6(npc_1_out_6));  // open: in_4
  PC pc_1 (.in_1(npc_1_out_5), .out_2(pc_1_out_2));
  IROM irom_1 (.in_1(pc_1_out_2), .out_2(irom_1_out_2));
  Multiplexer #(.select(2), .enable("false")) multiplexer_1 (
    .in0(npc_1_out_6), .in1(alu_1_out_5), .in2(sext_1_out_3), .in3(dram_1_out_4), .out(multiplexer_1_out));  // open: sel
  RF rf_1 (
    .in_1(irom_1_out_2), .in_2(irom_1_out_2), .in_3(multiplexer_1_out), .in_4(irom_1_out_2),
    .out_6(rf_1_out_6), .out_7(rf_1_out_7));  // open: in_5
  SEXT sext_1 (.in_1(irom_1_out_2), .out_3(sext_1_out_3));  // open: in_2
  Multiplexer #(.enable("false")) multiplexer_2 (
    .in0(pc_1_out_2), .in1(rf_1_out_6), .out(multiplexer_2_out));  // open: sel
  Multiplexer #(.enable("false")) multiplexer_3 (
    .in0(rf_1_out_7), .in1(sext_1_out_3), .out(multiplexer_3_out));  // open: sel
  ALU alu_1 (.in_2(multiplexer_2_out), .out_5(alu_1_out_5), .in_1(multiplexer_3_out));  // open: in_3, in_4
  DRAM dram_1 (.in_1(alu_1_out_5), .out_4(dram_1_out_4), .in_2(rf_1_out_7));  // open: in_3
endmodule

module PC (
  input  in_1,
  output out_2
);


  assign out_2 = in_1;
endmodule

module NPC (
  input  in_1,
  input  in_2,
  input  in_3,
  input  in_4,
  output out_5,
  output out_6
);
endmodule

module IROM (
  input  in_1,
  output out_2
);
endmodule

module CTRL (
  input  in_1,
  output out_2,
  output out_3,
  output out_4,
  output out_5,
  output out_6,
  output out_7,
  output out_8
);
endmodule

module DRAM (
  input  in_1,
  input  in_2,
  input  in_3,
  output out_4
);
endmodule

module ALU (
  input  in_1,
  input  in_2,
  input  in_3,
  input  in_4,
  output out_5
);
endmodule

module RF (
  input  in_1,
  input  in_2,
  input  in_3,
  input  in_4,
  input  in_5,
  output out_6,
  output out_7
);
endmodule

module SEXT (
  input  in_1,
  input  in_2,
  output out_3
);
endmodule
